# Fritzing sketch CNC_Pendant_v3 (saved by Fritzing 0.9.9b)
circuit board: 7.5cm x 7cm
breadboards: 1

parts:
  Arduino_Micro = Arduino Micro (Rev3)
  Mux = Analog Digital MUX Breakout
  Button_Connect = screw terminal, 14 pins
  S2 = Pushbutton [package="[THT]"]
  S3 = Pushbutton [package="[THT]"]
  S4 = Pushbutton [package="[THT]"]
  S5 = Pushbutton [package="[THT]"]
  S6 = Pushbutton [package="[THT]"]
  S7 = Pushbutton [package="[THT]"]
  S8 = Pushbutton [package="[THT]"]
  S9 = Pushbutton [package="[THT]"]
  S10 = Pushbutton [package="[THT]"]
  S11 = Pushbutton [package="[THT]"]
  S12 = Pushbutton [package="[THT]"]
  S13 = Pushbutton [package="[THT]"]
  S14 = Pushbutton [package="[THT]"]
  S15 = Pushbutton [package="[THT]"]
  Display_Conn = female pin header, 5 pins [form="♀ (female)"]
  Part3 = OLED Monochrome 128x64 1.3 inch [part_number=938]
  CNC_Enc_D7/D6 = KY-040 Rotary encoder [package=THT]
  Enc_Axis_D5/D4/D13 = KY-040 Rotary encoder [package=THT]
  Enc_Res_A0/A1/A2 = KY-040 Rotary encoder [package=THT]
  Enc_RPM_A3/A4/A5 = KY-040 Rotary encoder [package=THT]
  Enc_Conn = screw terminal, 12 pins
  Enc_GND/VCC = screw terminal, 12 pins

nets:
  N1: Arduino_Micro.RESET, Display_Conn.pin3, Part3.RESET
  N2: Arduino_Micro.D2/SDA, Display_Conn.pin4, Part3.MOSI_SDA
  N3: Arduino_Micro.D3/SCL, Display_Conn.pin5, Part3.SCLK_SCK
  N4: Arduino_Micro.D4_PWM/A6, Enc_Axis_D5/D4/D13.DT, Enc_Conn.pin9
  N5: Arduino_Micro.D5_PWM, Enc_Axis_D5/D4/D13.SW, Enc_Conn.pin10
  N6: Arduino_Micro.D6_PWM/A7, CNC_Enc_D7/D6.CLK, Enc_Conn.pin11
  N7: Arduino_Micro.D7, CNC_Enc_D7/D6.DT, Enc_Conn.pin12
  N8: Arduino_Micro.D8_PWM/A8, Mux.SIG
  N9: Arduino_Micro.D9_PWM/A9, Mux.S3
  N10: Arduino_Micro.D10_PWM/A10, Mux.S2
  N11: Arduino_Micro.D11_PWM, Mux.S1
  N12: Arduino_Micro.D12_PWM/A11, Mux.S0
  GND: Arduino_Micro.GND, Mux.GND, S2.Pin_3, S2.Pin_4, S3.Pin_3, S3.Pin_4, S4.Pin_3, S4.Pin_4, S5.Pin_3, S5.Pin_4, S6.Pin_3, S6.Pin_4, S7.Pin_3, S7.Pin_4, S8.Pin_3, S8.Pin_4, S9.Pin_3, S9.Pin_4, S10.Pin_3, S10.Pin_4, S11.Pin_3, S11.Pin_4, S12.Pin_3, S12.Pin_4, S13.Pin_3, S13.Pin_4, S14.Pin_3, S14.Pin_4, S15.Pin_3, S15.Pin_4, Display_Conn.pin1, Part3.GND, Enc_GND/VCC.pin1, Enc_GND/VCC.pin2, Enc_GND/VCC.pin3, Enc_GND/VCC.pin4, Enc_GND/VCC.pin5, Enc_GND/VCC.pin6
  VCC: Arduino_Micro.5V, Mux.VCC, Mux.EN, Display_Conn.pin2, Part3.VIN, CNC_Enc_D7/D6.Vcc, Enc_Axis_D5/D4/D13.Vcc, Enc_Res_A0/A1/A2.Vcc, Enc_RPM_A3/A4/A5.Vcc, Enc_GND/VCC.pin7, Enc_GND/VCC.pin8, Enc_GND/VCC.pin9, Enc_GND/VCC.pin10, Enc_GND/VCC.pin11, Enc_GND/VCC.pin12
  N13: Arduino_Micro.A5, Enc_RPM_A3/A4/A5.CLK, Enc_Conn.pin2
  N14: Arduino_Micro.A4, Enc_RPM_A3/A4/A5.DT, Enc_Conn.pin3
  N15: Arduino_Micro.A3, Enc_RPM_A3/A4/A5.SW, Enc_Conn.pin4
  N16: Arduino_Micro.A2, Enc_Res_A0/A1/A2.CLK, Enc_Conn.pin5
  N17: Arduino_Micro.A1, Enc_Res_A0/A1/A2.DT, Enc_Conn.pin6
  N18: Arduino_Micro.A0, Enc_Res_A0/A1/A2.SW, Enc_Conn.pin7
  N19: Arduino_Micro.D13_PWM, Enc_Axis_D5/D4/D13.CLK, Enc_Conn.pin8
  N20: Mux.C0, Button_Connect.pin14, S14.Pin_1, S14.Pin_2
  N21: Mux.C1, Button_Connect.pin13, S15.Pin_1, S15.Pin_2
  N22: Mux.C2, Button_Connect.pin12, S12.Pin_1, S12.Pin_2
  N23: Mux.C3, Button_Connect.pin11, S10.Pin_1, S10.Pin_2
  N24: Mux.C4, Button_Connect.pin10, S13.Pin_1, S13.Pin_2
  N25: Mux.C5, Button_Connect.pin9, S11.Pin_1, S11.Pin_2
  N26: Mux.C6, Button_Connect.pin8, S8.Pin_1, S8.Pin_2
  N27: Mux.C7, Button_Connect.pin7, S6.Pin_1, S6.Pin_2
  N28: Mux.C8, Button_Connect.pin6, S9.Pin_1, S9.Pin_2
  N29: Mux.C9, Button_Connect.pin5, S7.Pin_1, S7.Pin_2
  N30: Mux.C10, Button_Connect.pin4, S5.Pin_1, S5.Pin_2
  N31: Mux.C11, Button_Connect.pin3, S4.Pin_1, S4.Pin_2
  N32: Mux.C12, Button_Connect.pin2, S3.Pin_1, S3.Pin_2
  N33: Mux.C13, Button_Connect.pin1, S2.Pin_1, S2.Pin_2
  GND_2: CNC_Enc_D7/D6.GND, Enc_Axis_D5/D4/D13.GND, Enc_Res_A0/A1/A2.GND, Enc_RPM_A3/A4/A5.GND

custom parts:
  OLED Monochrome 128x64 1.3 inch: These displays are small, only about 1.3" diagonal, but very readable due to the high contrast of an OLED display. This display is made of 128x64 individual white OLED pixels, each one is turned on or off by the controller chip. Because the display makes its own light, no backlight is required. This reduces the power required to run the OLED and is why the display has such high contrast; we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
  KY-040 Rotary encoder: KY-040 Rotary Encoder with switch on breakout borad from AZ Delivery
